# Fritzing sketch diagram (saved by Fritzing 0.9.3b)

parts:
  Part1 = Arduino Uno (Rev3) - ICSP
  M1 = BTS7960
  M2 = DC Motor
  VCC1 = Battery block 9V

nets:
  N1: Part1.D2, M1.pin4
  N2: Part1.D3_PWM, M1.pin3
  N3: Part1.D5_PWM, M1.pin2
  N4: Part1.D6_PWM, M1.pin1
  N5: Part1.5V, M1.pin7
  N6: Part1.GND, M1.pin8
  N7: M1.pin9, M2.pin_1
  N8: M1.pin10, M2.pin_2
  N9: M1.pin11, VCC1.+
  N10: M1.pin12, VCC1.-

custom parts:
  BTS7960: BTS7960 43A Peak Power H-Bridge PWM Motor Driver
