# Fritzing sketch spld (saved by Fritzing 0.9.3b)

parts:
  Part1 = Arduino Uno (Rev3) - ICSP
  M1 = BTS7960
  Part2 = Thumb Joystick
  Part3 = Thumb Joystick
  M2 = DC Motor
  M3 = RioRand LM2596
  BAT1 = BC9VPC [package=bc9vpc]
  A1 = Adafruit v1.2 motor shield
  J1 = Basic Servo
  J2 = Basic Servo

nets:
  N1: Part1.A0, Part2.VERT
  N2: Part1.A1, Part2.HORZ
  N3: Part1.A2, Part3.VERT
  N4: Part1.A3, Part3.HORZ
  VCC: Part1.5V, M1.pin7, Part2.VCC, Part3.VCC, A1.Pin_10, A1.Pin_66, A1.Pin_69, J1.vcc, J2.vcc
  N5: Part1.D8, M1.pin4
  GND: Part1.GND, M1.pin8, Part2.GND, Part3.GND, A1.Pin_3, A1.Pin_11, A1.Pin_63, A1.Pin_67, A1.Pin_70, J1.gnd, J2.gnd
  N6: Part1.D5_PWM, M1.pin1
  N7: Part1.D6_PWM, M1.pin2
  N8: Part1.D7, M1.pin3
  N9: M1.pin9, M2.pin_1
  N10: M1.pin10, M2.pin_2
  N11: M1.pin11, M3.Pin_3
  N12: M1.pin12, M3.Pin_4
  N13: M3.Pin_1, BAT1.V+
  N14: M3.Pin_2, BAT1.V-
  N15: A1.Pin_65, J2.pulse
  N16: A1.Pin_68, J1.pulse

custom parts:
  BTS7960: BTS7960 43A Peak Power H-Bridge PWM Motor Driver
  Adafruit v1.2 motor shield: Adafruit v1.2 motor shield.
